# Fritzing sketch isef arm connections (saved by Fritzing 0.9.5d)
breadboards: 1

parts:
  MH-ET_LIVE_ESP32_DEVKIT3 = MH-ET LIVE ESP32 DEVKIT 38 pins
  J1 = Basic Servo
  J2 = Basic Servo
  J3 = Basic Servo
  J6 = Basic Servo
  J7 = Basic Servo
  J9 = Basic Servo
  J10 = Basic Servo

nets:
  N1: MH-ET_LIVE_ESP32_DEVKIT3.IO34, J7.pulse
  N2: MH-ET_LIVE_ESP32_DEVKIT3.IO35, J3.pulse
  N3: MH-ET_LIVE_ESP32_DEVKIT3.IO32, J2.pulse
  N4: MH-ET_LIVE_ESP32_DEVKIT3.IO33, J1.pulse
  N5: MH-ET_LIVE_ESP32_DEVKIT3.IO25, J9.pulse
  N6: MH-ET_LIVE_ESP32_DEVKIT3.IO26, J6.pulse
  N7: MH-ET_LIVE_ESP32_DEVKIT3.IO27, J10.pulse
  GND: MH-ET_LIVE_ESP32_DEVKIT3.GND#58, J1.gnd, J2.gnd, J3.gnd, J6.gnd, J7.gnd, J9.gnd, J10.gnd
  VCC: MH-ET_LIVE_ESP32_DEVKIT3.5V, J1.vcc, J2.vcc, J3.vcc, J6.vcc, J7.vcc, J9.vcc, J10.vcc

notes:
  Thumb finger (pin33)
  Index fingr
  (pin32)
  Middle finger(pin35)
  Little finger
  (pin34)
  SERVO 1 (Thumb)
  Ring finger
  (pin27)

custom parts:
  MH-ET LIVE ESP32 DEVKIT 38 pins: http://mh.nodebb.com/topic/2/mh-et-live-esp32-devkit
